# Fritzing sketch duinocoin_monitor_esp8266 (saved by Fritzing 0.9.4)
breadboards: 1

parts:
  OLED_I2C2 = OLED 128x64 I2C Monochrome Display
  U2 = ESP8266 NodeMCU LoLin module

nets:
  N1: OLED_I2C2.SDA, U2.D2
  N2: OLED_I2C2.SCK, U2.D1
  VDD: OLED_I2C2.VDD, U2.3V3
  GND: OLED_I2C2.GND, U2.GND

custom parts:
  ESP8266 NodeMCU LoLin module: ESP8266 based NodeMCU

// code stored in the sketch: duinocoin_monitor_esp8266.ino
#include <ESP8266WiFi.h>
#include <WiFiClientSecure.h>
#define ARDUINOJSON_USE_DOUBLE 1
#include <ArduinoJson.h>

const char* ssid = "";
const char* password = "";
const char* ducouser = "";
const char* host = "server.duinocoin.com";
const int httpsPort = 443;
const char* fingerprint = "72:D5:D1:06:8B:FA:8D:B3:0F:AF:3A:26:7C:F5:32:A2:A1:81:2A:28";
String url = "/users/" + String(ducouser);
const char* hostPrice = "raw.githubusercontent.com";
String urlPrice = "/revoxhere/duco-statistics/master/api.json";
const char* root_ca= \
"-----BEGIN CERTIFICATE-----\n" \
"MIIFLTCCBBWgAwIBAgISBLrlR4aCBlmofGjUwxvNkJ9IMA0GCSqGSIb3DQEBCwUA\n" \
"MDIxCzAJBgNVBAYTAlVTMRYwFAYDVQQKEw1MZXQncyBFbmNyeXB0MQswCQYDVQQD\n" \
"EwJSMzAeFw0yMTA0MjAxMjAwMThaFw0yMTA3MTkxMjAwMThaMB8xHTAbBgNVBAMT\n" \
"FHNlcnZlci5kdWlub2NvaW4uY29tMIIBIjANBgkqhkiG9w0BAQEFAAOCAQ8AMIIB\n" \
"CgKCAQEAv7SZV8V8uikoSOnw9KVa9M3HQsyB6l3QdinCuyZz7sRckOdSrUKtYFK/\n" \
"g+RmBqWVrwRLgnVmLtUlulHI7/H7Rbz0Exiv0beyjakd+p40O8V7Y1kuhE9z8WT6\n" \
"gtDd4grLNBMtUkd2Y8MmYFed2SP5OUoIdySdcUuo50NiS2KH5j3DhZB+ZmZn0lXw\n" \
"E91O2eNgEaryrnDoMftlJAUOSGh3uuCS27y1SXm8IC1Cxkv+OUyjXu9HnZoIX5v0\n" \
"59cTAFzrSo5tF/XtJlZ7fJU7VC98NaurfWKrF1XWgoKHJcjsFgep1K6PRIb7g5xq\n" \
"wlWUOFYTlDIYMAocGYJabw6jZrSphQIDAQABo4ICTjCCAkowDgYDVR0PAQH/BAQD\n" \
"AgWgMB0GA1UdJQQWMBQGCCsGAQUFBwMBBggrBgEFBQcDAjAMBgNVHRMBAf8EAjAA\n" \
"MB0GA1UdDgQWBBSGBC/8G5lAbUvFVjt4wL7kzsnzDjAfBgNVHSMEGDAWgBQULrMX\n" \
"t1hWy65QCUDmH6+dixTCxjBVBggrBgEFBQcBAQRJMEcwIQYIKwYBBQUHMAGGFWh0\n" \
"dHA6Ly9yMy5vLmxlbmNyLm9yZzAiBggrBgEFBQcwAoYWaHR0cDovL3IzLmkubGVu\n" \
"Y3Iub3JnLzAfBgNVHREEGDAWghRzZXJ2ZXIuZHVpbm9jb2luLmNvbTBMBgNVHSAE\n" \
"RTBDMAgGBmeBDAECATA3BgsrBgEEAYLfEwEBATAoMCYGCCsGAQUFBwIBFhpodHRw\n" \
"Oi8vY3BzLmxldHNlbmNyeXB0Lm9yZzCCAQMGCisGAQQB1nkCBAIEgfQEgfEA7wB2\n" \
"APZclC/RdzAiFFQYCDCUVo7jTRMZM7/fDC8gC8xO8WTjAAABeO9eAZAAAAQDAEcw\n" \
"RQIgXLdccQKNKjfPXVV1dbVW8LPmCKb80E8FOVBNw6WswN8CIQDerRKSvtgx4PxF\n" \
"1lOq8sFWwlMvchIkpiELDpmSQ7/6iAB1AFzcQ5L+5qtFRLFemtRW5hA3+9X6R9yh\n" \
"c5SyXub2xw7KAAABeO9eAYAAAAQDAEYwRAIgAkQ5SNxBduS8ckP7z0wEMMLdcNmf\n" \
"rR76s3MD8KIG/UQCIB4txuVGP/citMxxQYKFan1H0l4l2dYJuV4IAizWJ5GHMA0G\n" \
"CSqGSIb3DQEBCwUAA4IBAQCGELdxTgyUsqnCgE6bgOkRyAiVZHcSqNMg17DWw+ek\n" \
"IqfXFMbfuTFAs3+VRRCZS2BUiCttsmNzdiPIGgZLvyyv20RLDEjg7Kq22mudGg3F\n" \
"i/koB5DlGWWv9t2Ng/qnM/4+y6kAwpbJ8R1v4P3NpZgGFIccYgP+N41IOMT+OIzT\n" \
"6PxYyUH9yQx58e0t2FNTRjJSwIPZKfRUdLVIYb4sjXHqvLA9s76SkrUebDlEt16O\n" \
"vjDNTcK0q6jXGQjjRwjzPPmze36jvzhhGBypU3tXJifciRSl/4766tlvLwszMaOe\n" \
"yx+m+83OOchAq+N7/QxbXkNhAXrEzIOXOoYmA6QpfndQ\n" \
"-----END CERTIFICATE-----\n" \
"-----BEGIN CERTIFICATE-----\n" \
"MIIEZTCCA02gAwIBAgIQQAF1BIMUpMghjISpDBbN3zANBgkqhkiG9w0BAQsFADA/\n" \
"MSQwIgYDVQQKExtEaWdpdGFsIFNpZ25hdHVyZSBUcnVzdCBDby4xFzAVBgNVBAMT\n" \
"DkRTVCBSb290IENBIFgzMB4XDTIwMTAwNzE5MjE0MFoXDTIxMDkyOTE5MjE0MFow\n" \
"MjELMAkGA1UEBhMCVVMxFjAUBgNVBAoTDUxldCdzIEVuY3J5cHQxCzAJBgNVBAMT\n" \
"AlIzMIIBIjANBgkqhkiG9w0BAQEFAAOCAQ8AMIIBCgKCAQEAuwIVKMz2oJTTDxLs\n" \
"jVWSw/iC8ZmmekKIp10mqrUrucVMsa+Oa/l1yKPXD0eUFFU1V4yeqKI5GfWCPEKp\n" \
"Tm71O8Mu243AsFzzWTjn7c9p8FoLG77AlCQlh/o3cbMT5xys4Zvv2+Q7RVJFlqnB\n" \
"U840yFLuta7tj95gcOKlVKu2bQ6XpUA0ayvTvGbrZjR8+muLj1cpmfgwF126cm/7\n" \
"gcWt0oZYPRfH5wm78Sv3htzB2nFd1EbjzK0lwYi8YGd1ZrPxGPeiXOZT/zqItkel\n" \
"/xMY6pgJdz+dU/nPAeX1pnAXFK9jpP+Zs5Od3FOnBv5IhR2haa4ldbsTzFID9e1R\n" \
"oYvbFQIDAQABo4IBaDCCAWQwEgYDVR0TAQH/BAgwBgEB/wIBADAOBgNVHQ8BAf8E\n" \
"BAMCAYYwSwYIKwYBBQUHAQEEPzA9MDsGCCsGAQUFBzAChi9odHRwOi8vYXBwcy5p\n" \
"ZGVudHJ1c3QuY29tL3Jvb3RzL2RzdHJvb3RjYXgzLnA3YzAfBgNVHSMEGDAWgBTE\n" \
"p7Gkeyxx+tvhS5B1/8QVYIWJEDBUBgNVHSAETTBLMAgGBmeBDAECATA/BgsrBgEE\n" \
"AYLfEwEBATAwMC4GCCsGAQUFBwIBFiJodHRwOi8vY3BzLnJvb3QteDEubGV0c2Vu\n" \
"Y3J5cHQub3JnMDwGA1UdHwQ1MDMwMaAvoC2GK2h0dHA6Ly9jcmwuaWRlbnRydXN0\n" \
"LmNvbS9EU1RST09UQ0FYM0NSTC5jcmwwHQYDVR0OBBYEFBQusxe3WFbLrlAJQOYf\n" \
"r52LFMLGMB0GA1UdJQQWMBQGCCsGAQUFBwMBBggrBgEFBQcDAjANBgkqhkiG9w0B\n" \
"AQsFAAOCAQEA2UzgyfWEiDcx27sT4rP8i2tiEmxYt0l+PAK3qB8oYevO4C5z70kH\n" \
"ejWEHx2taPDY/laBL21/WKZuNTYQHHPD5b1tXgHXbnL7KqC401dk5VvCadTQsvd8\n" \
"S8MXjohyc9z9/G2948kLjmE6Flh9dDYrVYA9x2O+hEPGOaEOa1eePynBgPayvUfL\n" \
"qjBstzLhWVQLGAkXXmNs+5ZnPBxzDJOLxhF2JIbeQAcH5H0tZrUlo5ZYyOqA7s9p\n" \
"O5b85o3AM/OJ+CktFBQtfvBhcJVd9wvlwPsk+uyOy2HI7mNxKKgsBTt375teA2Tw\n" \
"UdHkhVNcsAKX1H7GNNLOEADksd86wuoXvg==\n" \
"-----END CERTIFICATE-----\n" \
"-----BEGIN CERTIFICATE-----\n" \
"MIIDSjCCAjKgAwIBAgIQRK+wgNajJ7qJMDmGLvhAazANBgkqhkiG9w0BAQUFADA/\n" \
"MSQwIgYDVQQKExtEaWdpdGFsIFNpZ25hdHVyZSBUcnVzdCBDby4xFzAVBgNVBAMT\n" \
"DkRTVCBSb290IENBIFgzMB4XDTAwMDkzMDIxMTIxOVoXDTIxMDkzMDE0MDExNVow\n" \
"PzEkMCIGA1UEChMbRGlnaXRhbCBTaWduYXR1cmUgVHJ1c3QgQ28uMRcwFQYDVQQD\n" \
"Ew5EU1QgUm9vdCBDQSBYMzCCASIwDQYJKoZIhvcNAQEBBQADggEPADCCAQoCggEB\n" \
"AN+v6ZdQCINXtMxiZfaQguzH0yxrMMpb7NnDfcdAwRgUi+DoM3ZJKuM/IUmTrE4O\n" \
"rz5Iy2Xu/NMhD2XSKtkyj4zl93ewEnu1lcCJo6m67XMuegwGMoOifooUMM0RoOEq\n" \
"OLl5CjH9UL2AZd+3UWODyOKIYepLYYHsUmu5ouJLGiifSKOeDNoJjj4XLh7dIN9b\n" \
"xiqKqy69cK3FCxolkHRyxXtqqzTWMIn/5WgTe1QLyNau7Fqckh49ZLOMxt+/yUFw\n" \
"7BZy1SbsOFU5Q9D8/RhcQPGX69Wam40dutolucbY38EVAjqr2m7xPi71XAicPNaD\n" \
"aeQQmxkqtilX4+U9m5/wAl0CAwEAAaNCMEAwDwYDVR0TAQH/BAUwAwEB/zAOBgNV\n" \
"HQ8BAf8EBAMCAQYwHQYDVR0OBBYEFMSnsaR7LHH62+FLkHX/xBVghYkQMA0GCSqG\n" \
"SIb3DQEBBQUAA4IBAQCjGiybFwBcqR7uKGY3Or+Dxz9LwwmglSBd49lZRNI+DT69\n" \
"ikugdB/OEIKcdBodfpga3csTS7MgROSR6cz8faXbauX+5v3gTt23ADq1cEmv8uXr\n" \
"AvHRAosZy5Q6XkjEGB5YGV8eAlrwDPGxrancWYaLbumR9YbK+rlmM6pZW87ipxZz\n" \
"R8srzJmwN0jP41ZL9c8PDHIyh8bwRLtTcm1D9SZImlJnt1ir/md2cXjbDaJWFBM5\n" \
"JDGFoqgCWjBH4d1QB7wCCZAA62RjYJsWvIjJEubSfZGL+T0yjWW06XyxV3bqxbYo\n" \
"Ob8VZRzI9neWagqNdwvYkQsEjgfbKbYK7p2CNTUQ\n" \
"-----END CERTIFICATE-----\n";

const char* root_revox = \
"-----BEGIN CERTIFICATE-----\n" \
"MIIHMDCCBhigAwIBAgIQAkk+B/qeN1otu8YdlEMPzzANBgkqhkiG9w0BAQsFADBw\n" \
"MQswCQYDVQQGEwJVUzEVMBMGA1UEChMMRGlnaUNlcnQgSW5jMRkwFwYDVQQLExB3\n" \
"d3cuZGlnaWNlcnQuY29tMS8wLQYDVQQDEyZEaWdpQ2VydCBTSEEyIEhpZ2ggQXNz\n" \
"dXJhbmNlIFNlcnZlciBDQTAeFw0yMDA1MDYwMDAwMDBaFw0yMjA0MTQxMjAwMDBa\n" \
"MGoxCzAJBgNVBAYTAlVTMRMwEQYDVQQIEwpDYWxpZm9ybmlhMRYwFAYDVQQHEw1T\n" \
"YW4gRnJhbmNpc2NvMRUwEwYDVQQKEwxHaXRIdWIsIEluYy4xFzAVBgNVBAMTDnd3\n" \
"dy5naXRodWIuY29tMIIBIjANBgkqhkiG9w0BAQEFAAOCAQ8AMIIBCgKCAQEAsj49\n" \
"6jJ99veEXO7WdxGQZ7idtCnDcjZqQeDiy6057SwXj9yDUVnqhwo/yII8+y6Jpk3g\n" \
"75LpPpYNjiOwYp/JkpWbpBAd1FWlvXJo/eZS+TwuIYb7JSc2H3NDDKt2VV5SSKQd\n" \
"XOkDNqq7BisOFp2/TYwCMZboLufwRR5fKxL0nTKIOCwpnH8k//UdWpvTgIixDGLY\n" \
"QCwHt0fYEo49jFeDaKD4WMBPq6Tx1iKWBhw3HVc/OyvI3yjRAx4Anf/DCSt9YTW6\n" \
"f/ND4O/fOowcfW5T7zii1Kw0yw+ulBrE/xe6taVhL+QR0MXNkQV2iHNN85swidwM\n" \
"tcdGI8g3fYL48bSRywIDAQABo4IDyjCCA8YwHwYDVR0jBBgwFoAUUWj/kK8CB3U8\n" \
"zNllZGKiErhZcjswHQYDVR0OBBYEFIygCmlH3IkysE3GEUViXxovlk46MHsGA1Ud\n" \
"EQR0MHKCDnd3dy5naXRodWIuY29tggwqLmdpdGh1Yi5jb22CCmdpdGh1Yi5jb22C\n" \
"CyouZ2l0aHViLmlvgglnaXRodWIuaW+CFyouZ2l0aHVidXNlcmNvbnRlbnQuY29t\n" \
"ghVnaXRodWJ1c2VyY29udGVudC5jb20wDgYDVR0PAQH/BAQDAgWgMB0GA1UdJQQW\n" \
"MBQGCCsGAQUFBwMBBggrBgEFBQcDAjB1BgNVHR8EbjBsMDSgMqAwhi5odHRwOi8v\n" \
"Y3JsMy5kaWdpY2VydC5jb20vc2hhMi1oYS1zZXJ2ZXItZzYuY3JsMDSgMqAwhi5o\n" \
"dHRwOi8vY3JsNC5kaWdpY2VydC5jb20vc2hhMi1oYS1zZXJ2ZXItZzYuY3JsMEwG\n" \
"A1UdIARFMEMwNwYJYIZIAYb9bAEBMCowKAYIKwYBBQUHAgEWHGh0dHBzOi8vd3d3\n" \
"LmRpZ2ljZXJ0LmNvbS9DUFMwCAYGZ4EMAQICMIGDBggrBgEFBQcBAQR3MHUwJAYI\n" \
"KwYBBQUHMAGGGGh0dHA6Ly9vY3NwLmRpZ2ljZXJ0LmNvbTBNBggrBgEFBQcwAoZB\n" \
"aHR0cDovL2NhY2VydHMuZGlnaWNlcnQuY29tL0RpZ2lDZXJ0U0hBMkhpZ2hBc3N1\n" \
"cmFuY2VTZXJ2ZXJDQS5jcnQwDAYDVR0TAQH/BAIwADCCAX0GCisGAQQB1nkCBAIE\n" \
"ggFtBIIBaQFnAHYARqVV63X6kSAwtaKJafTzfREsQXS+/Um4havy/HD+bUcAAAFx\n" \
"6y8fFgAABAMARzBFAiEA59y6w9oaoAoM2fvFq6KofYWRh0xRm4VEEaMHBtsBYUgC\n" \
"IBZxJhjA7SGWUlo57YslG8u6clHngDNvoTNVw1HQtTr3AHUAIkVFB1lVJFaWP6Ev\n" \
"8fdthuAjJmOtwEt/XcaDXG7iDwIAAAFx6y8evwAABAMARjBEAiBmEjiioTbc1//h\n" \
"CInYIX6O8hph5oLRVGCTxrTBfSRT2wIgZz7x3ZNIKQkWPKOFaaW3AxcB0DzhFsD6\n" \
"gxhkbl1p0AgAdgBRo7D1/QF5nFZtuDd4jwykeswbJ8v3nohCmg3+1IsF5QAAAXHr\n" \
"Lx8JAAAEAwBHMEUCIBQ/6El+TCCtWuop7IderN0+byn5sDreTu+Xz3GiY8cLAiEA\n" \
"7S83HxFFdQhQqpjjbWbIVBA88Nn/riaf5Jb8h3oJV8cwDQYJKoZIhvcNAQELBQAD\n" \
"ggEBAADzu/I/4dMPwG4QzMFHZmgQFlnc/xqXtaNLqONIzXPznBQmHQi481xKgAR4\n" \
"jZOTTknlwOLBXnDXvV6rJQZXut3pxHSvVJk2kvuyDO3RC0uudd81AXIUsd6Pnjt2\n" \
"D6Xd/ypUAoMkyE+8euYESEFk4HlnrpXtN7OSTGVYZQk0aJrDINslXdmUL9E6AQiI\n" \
"YaRIpRMRdj4stG6CkPJpfSauWa19kReZ6hTQR5f89L6x50us7GuWlmH6EmVFIbhf\n" \
"9EO02QA3CcU7bE1iLWMHmKcU6ythmgsvNRU5TikxvF77JFv7n1/y8GLrprmKpB6Q\n" \
"Df4PA8S9ROX9Rzgwe3KTIM6qeKU=\n" \
"-----END CERTIFICATE-----\n" \
"-----BEGIN CERTIFICATE-----\n" \
"MIIEsTCCA5mgAwIBAgIQBOHnpNxc8vNtwCtCuF0VnzANBgkqhkiG9w0BAQsFADBs\n" \
"MQswCQYDVQQGEwJVUzEVMBMGA1UEChMMRGlnaUNlcnQgSW5jMRkwFwYDVQQLExB3\n" \
"d3cuZGlnaWNlcnQuY29tMSswKQYDVQQDEyJEaWdpQ2VydCBIaWdoIEFzc3VyYW5j\n" \
"ZSBFViBSb290IENBMB4XDTEzMTAyMjEyMDAwMFoXDTI4MTAyMjEyMDAwMFowcDEL\n" \
"MAkGA1UEBhMCVVMxFTATBgNVBAoTDERpZ2lDZXJ0IEluYzEZMBcGA1UECxMQd3d3\n" \
"LmRpZ2ljZXJ0LmNvbTEvMC0GA1UEAxMmRGlnaUNlcnQgU0hBMiBIaWdoIEFzc3Vy\n" \
"YW5jZSBTZXJ2ZXIgQ0EwggEiMA0GCSqGSIb3DQEBAQUAA4IBDwAwggEKAoIBAQC2\n" \
"4C/CJAbIbQRf1+8KZAayfSImZRauQkCbztyfn3YHPsMwVYcZuU+UDlqUH1VWtMIC\n" \
"Kq/QmO4LQNfE0DtyyBSe75CxEamu0si4QzrZCwvV1ZX1QK/IHe1NnF9Xt4ZQaJn1\n" \
"itrSxwUfqJfJ3KSxgoQtxq2lnMcZgqaFD15EWCo3j/018QsIJzJa9buLnqS9UdAn\n" \
"4t07QjOjBSjEuyjMmqwrIw14xnvmXnG3Sj4I+4G3FhahnSMSTeXXkgisdaScus0X\n" \
"sh5ENWV/UyU50RwKmmMbGZJ0aAo3wsJSSMs5WqK24V3B3aAguCGikyZvFEohQcft\n" \
"bZvySC/zA/WiaJJTL17jAgMBAAGjggFJMIIBRTASBgNVHRMBAf8ECDAGAQH/AgEA\n" \
"MA4GA1UdDwEB/wQEAwIBhjAdBgNVHSUEFjAUBggrBgEFBQcDAQYIKwYBBQUHAwIw\n" \
"NAYIKwYBBQUHAQEEKDAmMCQGCCsGAQUFBzABhhhodHRwOi8vb2NzcC5kaWdpY2Vy\n" \
"dC5jb20wSwYDVR0fBEQwQjBAoD6gPIY6aHR0cDovL2NybDQuZGlnaWNlcnQuY29t\n" \
"L0RpZ2lDZXJ0SGlnaEFzc3VyYW5jZUVWUm9vdENBLmNybDA9BgNVHSAENjA0MDIG\n" \
"BFUdIAAwKjAoBggrBgEFBQcCARYcaHR0cHM6Ly93d3cuZGlnaWNlcnQuY29tL0NQ\n" \
"UzAdBgNVHQ4EFgQUUWj/kK8CB3U8zNllZGKiErhZcjswHwYDVR0jBBgwFoAUsT7D\n" \
"aQP4v0cB1JgmGggC72NkK8MwDQYJKoZIhvcNAQELBQADggEBABiKlYkD5m3fXPwd\n" \
"aOpKj4PWUS+Na0QWnqxj9dJubISZi6qBcYRb7TROsLd5kinMLYBq8I4g4Xmk/gNH\n" \
"E+r1hspZcX30BJZr01lYPf7TMSVcGDiEo+afgv2MW5gxTs14nhr9hctJqvIni5ly\n" \
"/D6q1UEL2tU2ob8cbkdJf17ZSHwD2f2LSaCYJkJA69aSEaRkCldUxPUd1gJea6zu\n" \
"xICaEnL6VpPX/78whQYwvwt/Tv9XBZ0k7YXDK/umdaisLRbvfXknsuvCnQsH6qqF\n" \
"0wGjIChBWUMo0oHjqvbsezt3tkBigAVBRQHvFwY+3sAzm2fTYS5yh+Rp/BIAV0Ae\n" \
"cPUeybQ=\n" \
"-----END CERTIFICATE-----\n" \
"-----BEGIN CERTIFICATE-----\n" \
"MIIDxTCCAq2gAwIBAgIQAqxcJmoLQJuPC3nyrkYldzANBgkqhkiG9w0BAQUFADBs\n" \
"MQswCQYDVQQGEwJVUzEVMBMGA1UEChMMRGlnaUNlcnQgSW5jMRkwFwYDVQQLExB3\n" \
"d3cuZGlnaWNlcnQuY29tMSswKQYDVQQDEyJEaWdpQ2VydCBIaWdoIEFzc3VyYW5j\n" \
"ZSBFViBSb290IENBMB4XDTA2MTExMDAwMDAwMFoXDTMxMTExMDAwMDAwMFowbDEL\n" \
"MAkGA1UEBhMCVVMxFTATBgNVBAoTDERpZ2lDZXJ0IEluYzEZMBcGA1UECxMQd3d3\n" \
"LmRpZ2ljZXJ0LmNvbTErMCkGA1UEAxMiRGlnaUNlcnQgSGlnaCBBc3N1cmFuY2Ug\n" \
"RVYgUm9vdCBDQTCCASIwDQYJKoZIhvcNAQEBBQADggEPADCCAQoCggEBAMbM5XPm\n" \
"+9S75S0tMqbf5YE/yc0lSbZxKsPVlDRnogocsF9ppkCxxLeyj9CYpKlBWTrT3JTW\n" \
"PNt0OKRKzE0lgvdKpVMSOO7zSW1xkX5jtqumX8OkhPhPYlG++MXs2ziS4wblCJEM\n" \
"xChBVfvLWokVfnHoNb9Ncgk9vjo4UFt3MRuNs8ckRZqnrG0AFFoEt7oT61EKmEFB\n" \
"Ik5lYYeBQVCmeVyJ3hlKV9Uu5l0cUyx+mM0aBhakaHPQNAQTXKFx01p8VdteZOE3\n" \
"hzBWBOURtCmAEvF5OYiiAhF8J2a3iLd48soKqDirCmTCv2ZdlYTBoSUeh10aUAsg\n" \
"EsxBu24LUTi4S8sCAwEAAaNjMGEwDgYDVR0PAQH/BAQDAgGGMA8GA1UdEwEB/wQF\n" \
"MAMBAf8wHQYDVR0OBBYEFLE+w2kD+L9HAdSYJhoIAu9jZCvDMB8GA1UdIwQYMBaA\n" \
"FLE+w2kD+L9HAdSYJhoIAu9jZCvDMA0GCSqGSIb3DQEBBQUAA4IBAQAcGgaX3Nec\n" \
"nzyIZgYIVyHbIUf4KmeqvxgydkAQV8GK83rZEWWONfqe/EW1ntlMMUu4kehDLI6z\n" \
"eM7b41N5cdblIZQB2lWHmiRk9opmzN6cN82oNLFpmyPInngiK3BD41VHMWEZ71jF\n" \
"hS9OMPagMRYjyOfiZRYzy78aG6A9+MpeizGLYAiJLQwGXFK3xPkKmNEVX58Svnw2\n" \
"Yzi9RKR/5CYrCsSXaQ3pjOLAEFe4yHYSkVXySGnYvCoCWw9E1CAx2/S6cCZdkGCe\n" \
"vEsXCS+0yx5DaMkHJ8HSXPfqIbloEpw8nL+e/IBcm2PN7EeqJSdnoDfzAIJ9VNep\n" \
"+OkuE6N36B9K\n" \
"-----END CERTIFICATE-----";

#define SDA_PIN 21
#define SCL_PIN 22
#define MAX_X 128
#define MAX_Y 64
#define screen_direction 0x3C
#include "SH1106.h"

SH1106 display(screen_direction, SDA_PIN, SCL_PIN);

uint32_t lastDrawTime;
uint32_t deauths = 0;       // deauth frames per second

int start;
int wait = 0;
int miners = 0;
float oldb = 0.0;
float userbalance;
float balance;
float ducomadesincesartdaily = 0.0;
float daily = 0;
String ducosmem;
String price;

void setup() {
  Serial.begin(115200);
  /* start screen */
  display.init();
  display.flipScreenVertically(); 
  display.setFont(ArialMT_Plain_10); 
  display.clear();
  display.drawString(6, 6, "Duinocoin Monitoring");
  display.drawString(24, 25, "Made by");
  display.drawString(29, 35, "tomaszafra.es");
  display.display();
  
  /* Connect */
  WiFi.begin(ssid, password); 
  while (WiFi.status() != WL_CONNECTED) {
    delay(500);
    Serial.println(".");
    display.drawString(6, 54, "Connecting ...");
    display.display();
  }
  display.clear();
  display.setFont(ArialMT_Plain_10);
  Serial.println(WiFi.localIP());
  display.drawString(6, 6, "Connected. IP: ");
  display.drawString(6, 24, WiFi.localIP().toString());
  display.display();
  start = millis();
  delay(2000);
}

void loop() {
  if ((WiFi.status() == WL_CONNECTED)) {
    WiFiClientSecure client;
    client.setInsecure();
    if (!client.connect(host, httpsPort)) {
      Serial.println("connection failed");
      return;
    }
    client.print(String("GET ") + url + " HTTP/1.1\r\n" +
               "Host: " + host + "\r\n" +
               "Connection: close\r\n\r\n");
    while (client.connected()) {
      String line = client.readStringUntil('\n');
      if (line == "\r") {
        display.clear();
        break;
      }
    }
    String jsonbalance = client.readStringUntil('\n');
    DynamicJsonDocument doc(3072);
    DeserializationError error = deserializeJson(doc, jsonbalance);
    if (error) {
      Serial.print(F("deserializeJson() failed: "));
      Serial.println(error.f_str());
      return;
    }
    JsonObject datadoc = doc.as<JsonObject>();
    String ducos = datadoc["result"]["balance"]["balance"];
    Serial.println(ducos);
    ducosmem = ducos;
    userbalance = ducos.toFloat();
    Serial.println("Ducos: " + String(ducos));
    
    // Miners
    miners = 0;
    for (JsonObject elem : datadoc["result"]["miners"].as<JsonArray>()) {
      miners++;
    }
    Serial.println("Miners: " + String(miners));
    doc.clear();
    client.stop();

    // Price
    client.setInsecure();
    if (!client.connect(hostPrice, httpsPort)) {
      Serial.println("connection failed");
      return;
    }
    client.print(String("GET ") + urlPrice + " HTTP/1.1\r\n" +
               "Host: " + hostPrice + "\r\n" +
               "Connection: close\r\n\r\n");
    while (client.connected()) {
      String line = client.readStringUntil('\n');
      if (line == "\r") {
        display.clear();
        break;
      }
    }
    String jsonprice = client.readString();
    DeserializationError errorPrice = deserializeJson(doc, jsonprice);
    if (errorPrice) {
      Serial.print(F("deserializeJson() failed: "));
      Serial.println(errorPrice.f_str());
      return;
    }
    JsonObject pricedoc = doc.as<JsonObject>();
    String euros = pricedoc["Duco price"];
    price = euros;
    Serial.println("Price: " + String(euros));
    doc.clear();
    client.stop();

    if(wait == 0){
        oldb = userbalance;
    } if(wait == 5){
        wait = 0;
        calcule_daily();
    } else{
        wait++;
    }
    
    display.clear();
    display.drawString(6, 6, "Ducos: " + String(ducosmem));
    display.drawString(6, 20, "Miners: " + String(miners));
    display.drawString(6, 34, "Daily: " + String(daily));
    display.drawString(6, 48, "Price: " + price);
    display.display();
  } else {
    display.clear();
    display.setFont(ArialMT_Plain_10);
    display.drawString(24, 34, "Connection lost");
    display.drawString(29, 44, "Reconnecting");
    display.display();
    WiFi.begin(ssid, password); 
    while (WiFi.status() != WL_CONNECTED) {
      delay(500);
      Serial.println(".");
      display.drawString(32, 6, ".");
      display.display();
    }
  }
  delay(15000);
}

void calcule_daily() {
  float ducomadein = userbalance - oldb;
  float dayduco = ducomadein * 960;
  daily = dayduco * 100 / 100;
  int ducomadesincestart = userbalance - balance;
  int secondssincestart = millis() - start;
  start = millis();
  ducomadesincesartdaily = ((86400/secondssincestart)*ducomadesincestart)*10 / 10;
}

// code stored in the sketch: ESP32_D1_package_monitoring.ino
/* uncomment if the default 4 bit mode doesn't work */
/* ------------------------------------------------ */
// #define BOARD_HAS_1BIT_SDMMC true // forces 1bit mode for SD MMC
/* ------------------------------------------------ */

#include "freertos/FreeRTOS.h"
#include "esp_wifi.h"
#include "esp_wifi_types.h"
#include "esp_system.h"
#include "esp_event.h"
#include "esp_event_loop.h"
#include "nvs_flash.h"
#include <stdio.h>
#include <string>
#include <cstddef>
#include <Wire.h>
#include <Preferences.h>
using namespace std;

/* ===== compile settings ===== */
#define MAX_CH 14       // 1 - 14 channels (1-11 for US, 1-13 for EU and 1-14 for Japan)
#define SNAP_LEN 2324   // max len of each recieved packet

#define BUTTON_PIN 5    // button to change the channel

#if CONFIG_FREERTOS_UNICORE
#define RUNNING_CORE 0
#else
#define RUNNING_CORE 1
#endif

#define USE_DISPLAY     // comment out if you don't want to use the OLED display
#define FLIP_DISPLAY    // comment out if you don't like to flip it
#define SDA_PIN 21
#define SCL_PIN 22
#define MAX_X 128
#define MAX_Y 64
#define screen_direction 0x3C

#ifdef USE_DISPLAY
#include "SH1106.h"
#endif

esp_err_t event_handler(void* ctx, system_event_t* event) {
  return ESP_OK;
}

#ifdef USE_DISPLAY
SH1106 display(screen_direction, SDA_PIN, SCL_PIN);
#endif

Preferences preferences;

bool buttonPressed = false;
bool buttonEnabled = true;
uint32_t lastDrawTime;
uint32_t lastButtonTime;
uint32_t tmpPacketCounter;
uint32_t pkts[MAX_X];       // here the packets per second will be saved
uint32_t deauths = 0;       // deauth frames per second
unsigned int ch = 1;        // current 802.11 channel
int rssiSum;

/* ===== functions ===== */
double getMultiplicator() {
  uint32_t maxVal = 1;
  for (int i = 0; i < MAX_X; i++) {
    if (pkts[i] > maxVal) maxVal = pkts[i];
  }
  if (maxVal > MAX_Y) return (double)MAX_Y / (double)maxVal;
  else return 1;
}

void setChannel(int newChannel) {
  ch = newChannel;
  if (ch > MAX_CH || ch < 1) ch = 1;

  preferences.begin("packetmonitor32", false);
  preferences.putUInt("channel", ch);
  preferences.end();

  esp_wifi_set_promiscuous(false);
  esp_wifi_set_channel(ch, WIFI_SECOND_CHAN_NONE);
  esp_wifi_set_promiscuous_rx_cb(&wifi_promiscuous);
  esp_wifi_set_promiscuous(true);
}

void wifi_promiscuous(void* buf, wifi_promiscuous_pkt_type_t type) {
  wifi_promiscuous_pkt_t* pkt = (wifi_promiscuous_pkt_t*)buf;
  wifi_pkt_rx_ctrl_t ctrl = (wifi_pkt_rx_ctrl_t)pkt->rx_ctrl;

  if (type == WIFI_PKT_MGMT && (pkt->payload[0] == 0xA0 || pkt->payload[0] == 0xC0 )) deauths++;

  if (type == WIFI_PKT_MISC) return;             // wrong packet type
  if (ctrl.sig_len > SNAP_LEN) return;           // packet too long

  uint32_t packetLength = ctrl.sig_len;
  if (type == WIFI_PKT_MGMT) packetLength -= 4;  // fix for known bug in the IDF https://github.com/espressif/esp-idf/issues/886

  //Serial.print(".");
  tmpPacketCounter++;
  rssiSum += ctrl.rssi;

}

void draw() {
  #ifdef USE_DISPLAY
    double multiplicator = getMultiplicator();
    int len;
    int rssi;

    if (pkts[MAX_X - 1] > 0) rssi = rssiSum / (int)pkts[MAX_X - 1];
    else rssi = rssiSum;

    display.clear();

    display.setTextAlignment(TEXT_ALIGN_RIGHT);
    display.drawString( 10, 0, (String)ch);
    display.drawString( 14, 0, ("|"));
    display.drawString( 30, 0, (String)rssi);
    display.drawString( 34, 0, ("|"));
    display.drawString( 82, 0, (String)tmpPacketCounter);
    display.drawString( 87, 0, ("["));
    display.drawString(106, 0, (String)deauths);
    display.drawString(110, 0, ("]"));
    display.drawString(114, 0, ("|"));
    display.setTextAlignment(TEXT_ALIGN_LEFT);
    display.drawString( 36,  0, ("Pkts:"));

    display.drawLine(0, 63 - MAX_Y, MAX_X, 63 - MAX_Y);
    for (int i = 0; i < MAX_X; i++) {
      len = pkts[i] * multiplicator;
      display.drawLine(i, 63, i, 63 - (len > MAX_Y ? MAX_Y : len));
      if (i < MAX_X - 1) pkts[i] = pkts[i + 1];
    }
    display.display();
  #endif
}

/* ===== main program ===== */
void setup() {

  // Serial
  Serial.begin(115200);

  // Settings
  preferences.begin("packetmonitor32", false);
  ch = preferences.getUInt("channel", 1);
  preferences.end();

  // System & WiFi
  nvs_flash_init();
  tcpip_adapter_init();
  wifi_init_config_t cfg = WIFI_INIT_CONFIG_DEFAULT();
  ESP_ERROR_CHECK(esp_event_loop_init(event_handler, NULL));
  ESP_ERROR_CHECK(esp_wifi_init(&cfg));
  //ESP_ERROR_CHECK(esp_wifi_set_country(WIFI_COUNTRY_EU));
  ESP_ERROR_CHECK(esp_wifi_set_storage(WIFI_STORAGE_RAM));
  ESP_ERROR_CHECK(esp_wifi_set_mode(WIFI_MODE_NULL));
  ESP_ERROR_CHECK(esp_wifi_start());

  esp_wifi_set_channel(ch, WIFI_SECOND_CHAN_NONE);

  // I/O
  pinMode(BUTTON_PIN, INPUT_PULLUP);

  // display
  #ifdef USE_DISPLAY
    display.init();
  #ifdef FLIP_DISPLAY
    display.flipScreenVertically();
  #endif
    /* show start screen */
    display.clear();
    display.setFont(ArialMT_Plain_16);
    display.drawString(6, 6, "PacketMonitor32");
    display.setFont(ArialMT_Plain_10);
    display.drawString(24, 34, "Made with <3 by");
    display.drawString(29, 44, "@Spacehuhn");
    display.display();

    delay(1000);
  #endif
  // second core
  xTaskCreatePinnedToCore(
    coreTask,               /* Function to implement the task */
    "coreTask",             /* Name of the task */
    2500,                   /* Stack size in words */
    NULL,                   /* Task input parameter */
    0,                      /* Priority of the task */
    NULL,                   /* Task handle. */
    RUNNING_CORE);          /* Core where the task should run */

  // start Wifi sniffer
  esp_wifi_set_promiscuous_rx_cb(&wifi_promiscuous);
  esp_wifi_set_promiscuous(true);
}

void loop() {
  vTaskDelay(portMAX_DELAY);
}

void coreTask( void * p ) {

  uint32_t currentTime;

  while (true) {

    currentTime = millis();

    /* bit of spaghetti code, have to clean this up later :D */

    // check button
    if (digitalRead(BUTTON_PIN) == LOW) {
      if (buttonEnabled) {
        if (!buttonPressed) {
          buttonPressed = true;
          lastButtonTime = currentTime;
        } else if (currentTime - lastButtonTime >= 2000) {
          draw();
          buttonPressed = false;
          buttonEnabled = false;
        }
      }
    } else {
      if (buttonPressed) {
        setChannel(ch + 1);
        draw();
      }
      buttonPressed = false;
      buttonEnabled = true;
    }


    // draw Display
    if ( currentTime - lastDrawTime > 1000 ) {
      lastDrawTime = currentTime;
      // Serial.printf("\nFree RAM %u %u\n", heap_caps_get_minimum_free_size(MALLOC_CAP_8BIT), heap_caps_get_minimum_free_size(MALLOC_CAP_32BIT));// for debug purposes

      pkts[MAX_X - 1] = tmpPacketCounter;

      draw();

      Serial.println((String)pkts[MAX_X - 1]);

      tmpPacketCounter = 0;
      deauths = 0;
      rssiSum = 0;
    }

    // Serial input
    if (Serial.available()) {
      ch = Serial.readString().toInt();
      if (ch < 1 || ch > 14) ch = 1;
      setChannel(ch);
    }

  }

}
